// Digital circuit 16to1from8to1multiplexer.dig as structural Verilog
module _16to1from8to1multiplexer (
  input  I0,
  input  I1,
  input  I2,
  input  I3,
  input  I4,
  input  I5,
  input  I6,
  input  I7,
  input  I8,
  input  I9,
  input  I10,
  input  I11,
  input  I12,
  input  I13,
  input  I14,
  input  I15,
  input  S0,
  input  S1,
  input  S2,
  input  S3,
  output O0
);

  wire _8to1multiplexer_1_o0, _8to1multiplexer_2_o0, not_1_out;

  not not_1 (not_1_out, S3);
  _8to1multiplexer _8to1multiplexer_1 (
    .S0(S0), .S1(S1), .S2(S2), .E(not_1_out), .I0(I0), .I1(I1), .I2(I2), .I3(I3), .I4(I4), .I5(I5), .I6(I6),
    .I7(I7), .O0(_8to1multiplexer_1_o0));
  _8to1multiplexer _8to1multiplexer_2 (
    .S0(S0), .S1(S1), .S2(S2), .E(S3), .I0(I8), .I1(I9), .I2(I10), .I3(I11), .I4(I12), .I5(I13), .I6(I14),
    .I7(I15), .O0(_8to1multiplexer_2_o0));
  or or_1 (O0, _8to1multiplexer_1_o0, _8to1multiplexer_2_o0);
endmodule
