// Digital circuit 16to4from8to3encoder.dig as structural Verilog
module _16to4from8to3encoder (
  input  I0,
  input  I1,
  input  I2,
  input  I3,
  input  I4,
  input  I5,
  input  I6,
  input  I7,
  input  I8,
  input  I9,
  input  I10,
  input  I11,
  input  I12,
  input  I13,
  input  I14,
  input  I15,
  output O0,
  output O1,
  output O2,
  output V,
  output O3
);

  wire _8to3encoder_1_o_0, _8to3encoder_1_o_1, _8to3encoder_1_o_2, _8to3encoder_1_v, _8to3encoder_2_o_0,
       _8to3encoder_2_o_1, _8to3encoder_2_o_2;

  _8to3encoder _8to3encoder_1 (
    .I_0(I0), .I_2(I1), .I_3(I2), .I_4(I3), .I_5(I4), .I_6(I5), .I_7(I6), .I_1(I7), .O_2(_8to3encoder_1_o_2),
    .O_1(_8to3encoder_1_o_1), .O_0(_8to3encoder_1_o_0), .V(_8to3encoder_1_v));
  _8to3encoder _8to3encoder_2 (
    .I_0(I8), .I_2(I9), .I_3(I10), .I_4(I11), .I_5(I12), .I_6(I13), .I_7(I14), .I_1(I15),
    .O_2(_8to3encoder_2_o_2), .O_1(_8to3encoder_2_o_1), .O_0(_8to3encoder_2_o_0), .V(O3));
  or or_1 (O0, _8to3encoder_1_o_2, _8to3encoder_2_o_2);
  or or_2 (O1, _8to3encoder_1_o_1, _8to3encoder_2_o_1);
  or or_3 (O2, _8to3encoder_1_o_0, _8to3encoder_2_o_0);
  or or_4 (V, _8to3encoder_1_v, O3);
endmodule
