// Digital circuit 3to8decoder.dig as structural Verilog
module _3to8decoder (
  input  E,
  input  I2,
  input  I1,
  input  I0,
  output O0,
  output O1,
  output O2,
  output O3,
  output O4,
  output O5,
  output O6,
  output O7
);

  wire not_1_out, not_2_out, not_3_out;

  not not_1 (not_1_out, I2);
  not not_2 (not_2_out, I1);
  not not_3 (not_3_out, I0);
  and and_1 (O0, E, not_3_out, not_2_out, not_1_out);
  and and_2 (O1, E, I0, not_2_out, not_1_out);
  and and_3 (O2, E, not_3_out, I1, not_1_out);
  and and_4 (O3, E, I0, I1, not_1_out);
  and and_5 (O4, E, not_3_out, not_2_out, I2);
  and and_6 (O5, E, I0, not_2_out, I2);
  and and_7 (O6, E, not_3_out, I1, I2);
  and and_8 (O7, E, I0, I1, I2);
endmodule
