// Digital circuit 4bitcarry_lookahead_adder.dig as structural Verilog
module _4bitcarry_lookahead_adder (
  input  A3,
  input  B3,
  input  A2,
  input  B2,
  input  A1,
  input  B1,
  input  A0,
  input  B0,
  input  Cin,
  output S0,
  output S1,
  output S2,
  output S3,
  output Cout
);

  wire and_1_out, and_2_out, and_3_out, and_4_out, and_5_out, and_6_out, and_7_out, and_8_out, or_1_out,
       or_2_out, or_3_out, or_4_out, or_5_out, or_6_out, or_7_out;

  and and_1 (and_1_out, A3, B3);
  or or_1 (or_1_out, A3, B3);
  and and_2 (and_2_out, A2, B2);
  or or_2 (or_2_out, A2, B2);
  and and_3 (and_3_out, A1, B1);
  or or_3 (or_3_out, A1, B1);
  and and_4 (and_4_out, A0, B0);
  or or_4 (or_4_out, A0, B0);
  xor xor_1 (S0, and_4_out, or_4_out, Cin);
  and and_5 (and_5_out, or_4_out, Cin);
  or or_5 (or_5_out, and_4_out, and_5_out);
  xor xor_2 (S1, or_5_out, and_3_out, or_3_out);
  and and_6 (and_6_out, or_3_out, or_5_out);
  or or_6 (or_6_out, and_3_out, and_6_out);
  xor xor_3 (S2, or_6_out, and_2_out, or_2_out);
  and and_7 (and_7_out, or_2_out, or_6_out);
  or or_7 (or_7_out, and_2_out, and_7_out);
  xor xor_4 (S3, or_7_out, and_1_out, or_1_out);
  and and_8 (and_8_out, or_1_out, or_7_out);
  or or_8 (Cout, and_1_out, and_8_out);
endmodule
