// Digital circuit 4to16from2to4decoder.dig as structural Verilog
module _4to16from2to4decoder (
  input  I3,
  input  I2,
  input  I1,
  input  I0,
  input  E,
  output O0,
  output O1,
  output O2,
  output O3,
  output O4,
  output O5,
  output O6,
  output O7,
  output O8,
  output O9,
  output O10,
  output O11,
  output O12,
  output O13,
  output O14,
  output O15
);

  wire _2to4decoder_1_o_0, _2to4decoder_1_o_1, _2to4decoder_1_o_2, _2to4decoder_1_o_3;

  _2to4decoder _2to4decoder_1 (
    .E(E), .I_0(I2), .I_1(I3), .O_0(_2to4decoder_1_o_0), .O_1(_2to4decoder_1_o_1), .O_2(_2to4decoder_1_o_2),
    .O_3(_2to4decoder_1_o_3));
  _2to4decoder _2to4decoder_2 (.E(_2to4decoder_1_o_0), .I_0(I0), .I_1(I1), .O_0(O0), .O_1(O1), .O_2(O2), .O_3(O3));
  _2to4decoder _2to4decoder_3 (.E(_2to4decoder_1_o_1), .I_0(I0), .I_1(I1), .O_0(O4), .O_1(O5), .O_2(O6), .O_3(O7));
  _2to4decoder _2to4decoder_4 (.E(_2to4decoder_1_o_2), .I_0(I0), .I_1(I1), .O_0(O8), .O_1(O9), .O_2(O10), .O_3(O11));
  _2to4decoder _2to4decoder_5 (.E(_2to4decoder_1_o_3), .I_0(I0), .I_1(I1), .O_0(O12), .O_1(O13), .O_2(O14), .O_3(O15));
endmodule
