// Digital circuit 8to1multiplexer.dig as structural Verilog
module _8to1multiplexer (
  input  S0,
  input  S1,
  input  S2,
  input  E,
  input  I0,
  input  I1,
  input  I2,
  input  I3,
  input  I4,
  input  I5,
  input  I6,
  input  I7,
  output O0
);

  wire and_1_out, and_2_out, and_3_out, and_4_out, and_5_out, and_6_out, and_7_out, and_8_out, not_1_out,
       not_2_out, not_3_out, or_1_out, or_2_out;

  not not_1 (not_1_out, S2);
  not not_2 (not_2_out, S1);
  not not_3 (not_3_out, S0);
  and and_1 (and_1_out, not_3_out, not_2_out, I0, not_1_out, E);
  and and_2 (and_2_out, S0, not_2_out, I1, not_1_out, E);
  and and_3 (and_3_out, not_3_out, S1, I2, not_1_out, E);
  and and_4 (and_4_out, S0, S1, I3, not_1_out, E);
  and and_5 (and_5_out, not_3_out, not_2_out, I4, S2, E);
  and and_6 (and_6_out, S0, not_2_out, I5, S2, E);
  and and_7 (and_7_out, not_3_out, S1, I6, S2, E);
  and and_8 (and_8_out, S0, S1, I7, S2, E);
  or or_1 (or_1_out, and_1_out, and_2_out, and_3_out, and_4_out);
  or or_2 (or_2_out, and_5_out, and_6_out, and_7_out, and_8_out);
  or or_3 (O0, or_1_out, or_2_out);
endmodule
